# Fritzing sketch ImprobDrive (saved by Fritzing 0.9.3b)
breadboards: 1

parts:
  Part1 = Arduino Uno (Rev3)
  R2 = Slide Potentiometer [maximum_resistance=100kΩ]
  LED1 = LED - 5mm [color="Red (633nm)" package="5 mm [THT]"]
  LED2 = LED - 5mm [color="Yellow (585nm)" package="5 mm [THT]"]
  LED3 = LED - 5mm [color="Yellow (585nm)" package="5 mm [THT]"]
  LED4 = LED - 5mm [color="Yellow (585nm)" package="5 mm [THT]"]
  LED5 = LED - 5mm [color="Green (560nm)" package="5 mm [THT]"]
  LED6 = LED - 5mm [color="Green (560nm)" package="5 mm [THT]"]
  LED7 = LED - 5mm [color="Green (560nm)" package="5 mm [THT]"]
  LED8 = LED - 5mm [color="Green (560nm)" package="5 mm [THT]"]
  R3 = Resistor [tolerance=±5% resistance=220 package=THT]
  R4 = Resistor [tolerance=±5% resistance=220 package=THT]
  R5 = Resistor [tolerance=±5% resistance=220 package=THT]
  R6 = Resistor [tolerance=±5% resistance=220 package=THT]
  R7 = Resistor [tolerance=±5% resistance=220 package=THT]
  R8 = Resistor [tolerance=±5% resistance=220 package=THT]
  R9 = Resistor [tolerance=±5% resistance=220 package=THT]
  R10 = Resistor [tolerance=±5% resistance=220 package=THT]

nets:
  N1: Part1.A0, R2.leg1
  N2: Part1.GND, R2.wiper, LED1.cathode, LED2.cathode, LED3.cathode, LED4.cathode, LED5.cathode, LED6.cathode, LED7.cathode, LED8.cathode
  N3: Part1.D0/RX, R10.Pin_0
  N4: Part1.D1/TX, R9.Pin_0
  N5: Part1.D2, R8.Pin_0
  N6: Part1.D3_PWM, R7.Pin_0
  N7: Part1.D4, R6.Pin_0
  N8: Part1.D5_PWM, R5.Pin_0
  N9: Part1.D6_PWM, R4.Pin_0
  N10: Part1.D7, R3.Pin_0
  N11: Part1.5V, R2.leg2
  N12: LED1.anode, R3.Pin_1
  N13: LED2.anode, R4.Pin_1
  N14: LED3.anode, R5.Pin_1
  N15: LED4.anode, R6.Pin_1
  N16: LED5.anode, R7.Pin_1
  N17: LED6.anode, R8.Pin_1
  N18: LED7.anode, R9.Pin_1
  N19: LED8.anode, R10.Pin_1
